// Digital circuit B.R.dig as structural Verilog
module B_R (
  input  W,
  input  Clk,
  input  [31:0] In,
  input  [3:0] Endw,
  input  [3:0] End_Ra,
  input  [3:0] End_Rb,
  output [31:0] Out_0,
  output [31:0] Out1
);

  wire r0_i, r1_i, r2_i, r3_i, r4_i, r5_i, r6_i, r7_i, r8_i, r9_i, r10_i, r11_i, r12_i, r13_i, r14_i, r15_i;
  wire [31:0] multiplexer_1_out, multiplexer_2_out, multiplexer_3_out, multiplexer_4_out, multiplexer_5_out,
       multiplexer_6_out, multiplexer_7_out, multiplexer_8_out, multiplexer_9_out, multiplexer_10_out,
       multiplexer_11_out, multiplexer_12_out, multiplexer_13_out, multiplexer_14_out, multiplexer_15_out,
       multiplexer_16_out, r0_o, r1_o, r2_o, r3_o, r4_o, r5_o, r6_o, r7_o, r8_o, r9_o, r10_o, r11_o, r12_o,
       r13_o, r14_o, r15_o;

  Demultiplexer #(.Selector_Bits(4)) demultiplexer_1 (
    .sel(Endw), .in(W), .out_0(r0_i), .out_1(r1_i), .out_2(r2_i), .out_3(r3_i), .out_4(r4_i), .out_5(r5_i),
    .out_6(r6_i), .out_7(r7_i), .out_8(r8_i), .out_9(r9_i), .out_10(r10_i), .out_11(r11_i), .out_12(r12_i),
    .out_13(r13_i), .out_14(r14_i), .out_15(r15_i));
  Multiplexer #(.Bits(32)) multiplexer_1 (.sel(r0_i), .in_0(r0_o), .in_1(r0_o), .out(multiplexer_1_out));
  Multiplexer #(.Bits(32)) multiplexer_2 (.sel(r4_i), .in_0(r4_o), .in_1(In), .out(multiplexer_2_out));
  Multiplexer #(.Bits(32)) multiplexer_3 (.sel(r8_i), .in_0(r8_o), .in_1(In), .out(multiplexer_3_out));
  Multiplexer #(.Bits(32)) multiplexer_4 (.sel(r12_i), .in_0(r12_o), .in_1(In), .out(multiplexer_4_out));
  Registrador _0 (.Clk(Clk), .In(multiplexer_1_out), .Out(r0_o));
  Registrador _4 (.Clk(Clk), .In(multiplexer_2_out), .Out(r4_o));
  Registrador _8 (.Clk(Clk), .In(multiplexer_3_out), .Out(r8_o));
  Registrador _12 (.Clk(Clk), .In(multiplexer_4_out), .Out(r12_o));
  Multiplexer #(.Bits(32)) multiplexer_5 (.sel(r1_i), .in_0(r1_o), .in_1(In), .out(multiplexer_5_out));
  Multiplexer #(.Bits(32)) multiplexer_6 (.sel(r5_i), .in_0(r5_o), .in_1(In), .out(multiplexer_6_out));
  Multiplexer #(.Bits(32)) multiplexer_7 (.sel(r9_i), .in_0(r9_o), .in_1(In), .out(multiplexer_7_out));
  Multiplexer #(.Bits(32)) multiplexer_8 (.sel(r13_i), .in_0(r13_o), .in_1(In), .out(multiplexer_8_out));
  Registrador _1 (.Clk(Clk), .In(multiplexer_5_out), .Out(r1_o));
  Registrador _5 (.Clk(Clk), .In(multiplexer_6_out), .Out(r5_o));
  Registrador _9 (.Clk(Clk), .In(multiplexer_7_out), .Out(r9_o));
  Registrador _13 (.Clk(Clk), .In(multiplexer_8_out), .Out(r13_o));
  Multiplexer #(.Bits(32)) multiplexer_9 (.sel(r2_i), .in_0(r2_o), .in_1(In), .out(multiplexer_9_out));
  Multiplexer #(.Bits(32)) multiplexer_10 (.sel(r6_i), .in_0(r6_o), .in_1(In), .out(multiplexer_10_out));
  Multiplexer #(.Bits(32)) multiplexer_11 (.sel(r10_i), .in_0(r10_o), .in_1(In), .out(multiplexer_11_out));
  Multiplexer #(.Bits(32)) multiplexer_12 (.sel(r14_i), .in_0(r14_o), .in_1(In), .out(multiplexer_12_out));
  Registrador _2 (.Clk(Clk), .In(multiplexer_9_out), .Out(r2_o));
  Registrador _6 (.Clk(Clk), .In(multiplexer_10_out), .Out(r6_o));
  Registrador _10 (.Clk(Clk), .In(multiplexer_11_out), .Out(r10_o));
  Registrador _14 (.Clk(Clk), .In(multiplexer_12_out), .Out(r14_o));
  Multiplexer #(.Bits(32)) multiplexer_13 (.sel(r3_i), .in_0(r3_o), .in_1(In), .out(multiplexer_13_out));
  Multiplexer #(.Bits(32)) multiplexer_14 (.sel(r7_i), .in_0(r7_o), .in_1(In), .out(multiplexer_14_out));
  Multiplexer #(.Bits(32)) multiplexer_15 (.sel(r11_i), .in_0(r11_o), .in_1(In), .out(multiplexer_15_out));
  Multiplexer #(.Bits(32)) multiplexer_16 (.sel(r15_i), .in_0(r15_o), .in_1(In), .out(multiplexer_16_out));
  Registrador _3 (.Clk(Clk), .In(multiplexer_13_out), .Out(r3_o));
  Registrador _7 (.Clk(Clk), .In(multiplexer_14_out), .Out(r7_o));
  Registrador _11 (.Clk(Clk), .In(multiplexer_15_out), .Out(r11_o));
  Registrador _15 (.Clk(Clk), .In(multiplexer_16_out), .Out(r15_o));
  Multiplexer #(.Selector_Bits(4), .Bits(32)) multiplexer_17 (
    .sel(End_Ra), .in_0(r0_o), .in_1(r1_o), .in_2(r2_o), .in_3(r3_o), .in_4(r4_o), .in_5(r5_o), .in_6(r6_o),
    .in_7(r7_o), .in_8(r8_o), .in_9(r9_o), .in_10(r10_o), .in_11(r11_o), .in_12(r12_o), .in_13(r13_o),
    .in_14(r14_o), .in_15(r15_o), .out(Out_0));
  Multiplexer #(.Selector_Bits(4), .Bits(32)) multiplexer_18 (
    .sel(End_Rb), .in_0(r0_o), .in_1(r1_o), .in_2(r2_o), .in_3(r3_o), .in_4(r4_o), .in_5(r5_o), .in_6(r6_o),
    .in_7(r7_o), .in_8(r8_o), .in_9(r9_o), .in_10(r10_o), .in_11(r11_o), .in_12(r12_o), .in_13(r13_o),
    .in_14(r14_o), .in_15(r15_o), .out(Out1));
endmodule
