// Digital circuit Full_Adder.dig as structural Verilog
module Full_Adder (
  input  A,
  input  B,
  input  Ci,
  output S,
  output Co
);

  wire and_1_out, and_2_out, xor_1_out;

  xor xor_1 (xor_1_out, B, A);
  and and_1 (and_1_out, B, A);
  and and_2 (and_2_out, xor_1_out, Ci);
  xor xor_2 (S, xor_1_out, Ci);
  or or_1 (Co, and_2_out, and_1_out);
endmodule
