// Digital circuit Full_Adder_24bits.dig as structural Verilog
module Full_Adder_24bits (
  input  [23:0] A,
  input  [23:0] B,
  output [23:0] C
);

  wire full_adder_4bits_1_cout, full_adder_4bits_2_cout, full_adder_4bits_3_cout, full_adder_4bits_4_cout,
       full_adder_4bits_iniciais_1_cout;

  full_adder_4bits_iniciais full_adder_4bits_iniciais_1 (
    .S0(C[0]), .S1(C[1]), .S2(C[2]), .S3(C[3]), .Cout(full_adder_4bits_iniciais_1_cout), .A(A[3:0]),
    .B(B[3:0]));
  full_adder_4bits full_adder_4bits_1 (
    .S0(C[4]), .S1(C[5]), .S2(C[6]), .S3(C[7]), .Cout(full_adder_4bits_1_cout),
    .Cin(full_adder_4bits_iniciais_1_cout), .A(A[7:4]), .B(B[7:4]));
  full_adder_4bits full_adder_4bits_2 (
    .S0(C[8]), .S1(C[9]), .S2(C[10]), .S3(C[11]), .Cout(full_adder_4bits_2_cout),
    .Cin(full_adder_4bits_1_cout), .A(A[11:8]), .B(B[11:8]));
  full_adder_4bits full_adder_4bits_3 (
    .S0(C[12]), .S1(C[13]), .S2(C[14]), .S3(C[15]), .Cout(full_adder_4bits_3_cout),
    .Cin(full_adder_4bits_2_cout), .A(A[15:12]), .B(B[15:12]));
  full_adder_4bits full_adder_4bits_4 (
    .S0(C[16]), .S1(C[17]), .S2(C[18]), .S3(C[19]), .Cout(full_adder_4bits_4_cout),
    .Cin(full_adder_4bits_3_cout), .A(A[19:16]), .B(B[19:16]));
  full_adder_4bits_finais full_adder_4bits_finais_1 (
    .S0(C[20]), .S1(C[21]), .S2(C[22]), .S3(C[23]), .Cin(full_adder_4bits_4_cout), .A(A[23:20]), .B(B[23:20]));

  // Other names for the same wires on the sheet: _3[3:0] = C[15:12]; _4[3:0] = C[19:16]; _5[3:0] = C[23:20];
  //   _2[3:0] = C[11:8]; _1[3:0] = C[7:4]; _0[3:0] = C[3:0]
endmodule
