// Digital circuit Registrador.dig as structural Verilog
module Registrador (
  input  Clk,
  input  [31:0] In,
  output [31:0] Out
);

  D_FF d_ff_1 (.D(In[0]), .C(Clk), .Q(Out[0]));  // open: nQ
  D_FF d_ff_2 (.D(In[1]), .C(Clk), .Q(Out[1]));  // open: nQ
  D_FF d_ff_3 (.D(In[2]), .C(Clk), .Q(Out[2]));  // open: nQ
  D_FF d_ff_4 (.D(In[3]), .C(Clk), .Q(Out[3]));  // open: nQ
  D_FF d_ff_5 (.D(In[4]), .C(Clk), .Q(Out[4]));  // open: nQ
  D_FF d_ff_6 (.D(In[5]), .C(Clk), .Q(Out[5]));  // open: nQ
  D_FF d_ff_7 (.D(In[6]), .C(Clk), .Q(Out[6]));  // open: nQ
  D_FF d_ff_8 (.D(In[7]), .C(Clk), .Q(Out[7]));  // open: nQ
  D_FF d_ff_9 (.D(In[8]), .C(Clk), .Q(Out[8]));  // open: nQ
  D_FF d_ff_10 (.D(In[9]), .C(Clk), .Q(Out[9]));  // open: nQ
  D_FF d_ff_11 (.D(In[10]), .C(Clk), .Q(Out[10]));  // open: nQ
  D_FF d_ff_12 (.D(In[11]), .C(Clk), .Q(Out[11]));  // open: nQ
  D_FF d_ff_13 (.D(In[12]), .C(Clk), .Q(Out[12]));  // open: nQ
  D_FF d_ff_14 (.D(In[13]), .C(Clk), .Q(Out[13]));  // open: nQ
  D_FF d_ff_15 (.D(In[14]), .C(Clk), .Q(Out[14]));  // open: nQ
  D_FF d_ff_16 (.D(In[15]), .C(Clk), .Q(Out[15]));  // open: nQ
  D_FF d_ff_17 (.D(In[16]), .C(Clk), .Q(Out[16]));  // open: nQ
  D_FF d_ff_18 (.D(In[17]), .C(Clk), .Q(Out[17]));  // open: nQ
  D_FF d_ff_19 (.D(In[18]), .C(Clk), .Q(Out[18]));  // open: nQ
  D_FF d_ff_20 (.D(In[19]), .C(Clk), .Q(Out[19]));  // open: nQ
  D_FF d_ff_21 (.D(In[20]), .C(Clk), .Q(Out[20]));  // open: nQ
  D_FF d_ff_22 (.D(In[21]), .C(Clk), .Q(Out[21]));  // open: nQ
  D_FF d_ff_23 (.D(In[22]), .C(Clk), .Q(Out[22]));  // open: nQ
  D_FF d_ff_24 (.D(In[23]), .C(Clk), .Q(Out[23]));  // open: nQ
  D_FF d_ff_25 (.D(In[24]), .C(Clk), .Q(Out[24]));  // open: nQ
  D_FF d_ff_26 (.D(In[25]), .C(Clk), .Q(Out[25]));  // open: nQ
  D_FF d_ff_27 (.D(In[26]), .C(Clk), .Q(Out[26]));  // open: nQ
  D_FF d_ff_28 (.D(In[27]), .C(Clk), .Q(Out[27]));  // open: nQ
  D_FF d_ff_29 (.D(In[28]), .C(Clk), .Q(Out[28]));  // open: nQ
  D_FF d_ff_30 (.D(In[29]), .C(Clk), .Q(Out[29]));  // open: nQ
  D_FF d_ff_31 (.D(In[30]), .C(Clk), .Q(Out[30]));  // open: nQ
  D_FF d_ff_32 (.D(In[31]), .C(Clk), .Q(Out[31]));  // open: nQ
endmodule
