// Digital circuit ULA.dig as structural Verilog
module ULA (
  input  [31:0] A,
  input  [31:0] B,
  input  [2:0] Seletor,
  output [31:0] C,
  output Zero
);

  wire [31:0] and_1_out, full_adder_completo_1_s31, or_1_out, shifter_1_c, subtrator_1_s31, xor_1_out;
  wire [63:0] mul_1_mul;

  shifter shifter_1 (.A(A), .B(B), .C(shifter_1_c));
  assign xor_1_out = A ^ B;  // XOr xor_1, 32 bits wide
  assign or_1_out = A | B;  // Or or_1, 32 bits wide
  assign and_1_out = A & B;  // And and_1, 32 bits wide
  Mul #(.Signed("true"), .Bits(32)) mul_1 (.a(A), .b(B), .mul(mul_1_mul));
  subtrator subtrator_1 (
    .A(A), .B(B), .S0(subtrator_1_s31[0]), .S1(subtrator_1_s31[1]), .S2(subtrator_1_s31[2]),
    .S3(subtrator_1_s31[3]), .S4(subtrator_1_s31[4]), .S5(subtrator_1_s31[5]), .S6(subtrator_1_s31[6]),
    .S7(subtrator_1_s31[7]), .S8(subtrator_1_s31[8]), .S9(subtrator_1_s31[9]), .S10(subtrator_1_s31[10]),
    .S11(subtrator_1_s31[11]), .S12(subtrator_1_s31[12]), .S13(subtrator_1_s31[13]),
    .S14(subtrator_1_s31[14]), .S15(subtrator_1_s31[15]), .S16(subtrator_1_s31[16]),
    .S17(subtrator_1_s31[17]), .S18(subtrator_1_s31[18]), .S19(subtrator_1_s31[19]),
    .S20(subtrator_1_s31[20]), .S21(subtrator_1_s31[21]), .S22(subtrator_1_s31[22]),
    .S23(subtrator_1_s31[23]), .S24(subtrator_1_s31[24]), .S25(subtrator_1_s31[25]),
    .S26(subtrator_1_s31[26]), .S27(subtrator_1_s31[27]), .S28(subtrator_1_s31[28]),
    .S29(subtrator_1_s31[29]), .S30(subtrator_1_s31[30]), .S31(subtrator_1_s31[31]));
  Multiplexer #(.Selector_Bits(3), .Bits(32)) multiplexer_1 (
    .sel(Seletor), .in_0(full_adder_completo_1_s31), .in_1(subtrator_1_s31), .in_2(mul_1_mul[31:0]),
    .in_3(and_1_out), .in_4(or_1_out), .in_5(xor_1_out), .in_6(shifter_1_c), .in_7({32{1'b0}}), .out(C));
  full_adder_completo full_adder_completo_1 (
    .A(A), .B(B), .S0(full_adder_completo_1_s31[0]), .S1(full_adder_completo_1_s31[1]),
    .S2(full_adder_completo_1_s31[2]), .S3(full_adder_completo_1_s31[3]), .S4(full_adder_completo_1_s31[4]),
    .S5(full_adder_completo_1_s31[5]), .S6(full_adder_completo_1_s31[6]), .S7(full_adder_completo_1_s31[7]),
    .S8(full_adder_completo_1_s31[8]), .S9(full_adder_completo_1_s31[9]),
    .S10(full_adder_completo_1_s31[10]), .S11(full_adder_completo_1_s31[11]),
    .S12(full_adder_completo_1_s31[12]), .S13(full_adder_completo_1_s31[13]),
    .S14(full_adder_completo_1_s31[14]), .S15(full_adder_completo_1_s31[15]),
    .S16(full_adder_completo_1_s31[16]), .S17(full_adder_completo_1_s31[17]),
    .S18(full_adder_completo_1_s31[18]), .S19(full_adder_completo_1_s31[19]),
    .S20(full_adder_completo_1_s31[20]), .S21(full_adder_completo_1_s31[21]),
    .S22(full_adder_completo_1_s31[22]), .S23(full_adder_completo_1_s31[23]),
    .S24(full_adder_completo_1_s31[24]), .S25(full_adder_completo_1_s31[25]),
    .S26(full_adder_completo_1_s31[26]), .S27(full_adder_completo_1_s31[27]),
    .S28(full_adder_completo_1_s31[28]), .S29(full_adder_completo_1_s31[29]),
    .S30(full_adder_completo_1_s31[30]), .S31(full_adder_completo_1_s31[31]));
  nor nor_1 (Zero, C[0], C[1], C[2], C[3], C[4], C[5], C[6], C[7], C[8], C[9], C[10], C[11], C[12], C[13], C[14], C[15], C[16], C[17], C[18], C[19], C[20], C[21], C[22], C[23], C[24], C[25], C[26], C[27], C[28], C[29], C[30], C[31]);
endmodule
