// Digital circuit ext_zero.dig as structural Verilog
module ext_zero (
  input  [15:0] _16,
  output [31:0] _32
);

  wire not_1_out;

  not not_1 (not_1_out, _16[15]);
  and and_1 (_32[31], _16[15], not_1_out);

  assign _32[30:0] = {{16{_32[31]}}, _16[14:0]};
endmodule
