// Digital circuit full_adder_4bits_iniciais.dig as structural Verilog
module full_adder_4bits_iniciais (
  input  [3:0] A,
  input  [3:0] B,
  output S0,
  output S1,
  output S2,
  output S3,
  output Cout
);

  wire full_adder_1_co, full_adder_2_co, half_adder_1_c;

  Half_Adder half_adder_1 (.A(A[0]), .B(B[0]), .S(S0), .C(half_adder_1_c));
  Full_Adder full_adder_1 (.A(A[1]), .B(B[1]), .Ci(half_adder_1_c), .S(S1), .Co(full_adder_1_co));
  Full_Adder full_adder_2 (.A(A[2]), .B(B[2]), .Ci(full_adder_1_co), .S(S2), .Co(full_adder_2_co));
  Full_Adder full_adder_3 (.A(A[3]), .B(B[3]), .Ci(full_adder_2_co), .S(S3), .Co(Cout));
endmodule
