// Digital circuit full_adder_completo.dig as structural Verilog
module full_adder_completo (
  input  [31:0] A,
  input  [31:0] B,
  output S0,
  output S1,
  output S2,
  output S3,
  output S4,
  output S5,
  output S6,
  output S7,
  output S8,
  output S9,
  output S10,
  output S11,
  output S12,
  output S13,
  output S14,
  output S15,
  output S16,
  output S17,
  output S18,
  output S19,
  output S20,
  output S21,
  output S22,
  output S23,
  output S24,
  output S25,
  output S26,
  output S27,
  output S28,
  output S29,
  output S30,
  output S31
);

  wire full_adder_4bits_1_cout, full_adder_4bits_2_cout, full_adder_4bits_3_cout, full_adder_4bits_4_cout,
       full_adder_4bits_5_cout, full_adder_4bits_6_cout, full_adder_4bits_iniciais_1_cout;

  full_adder_4bits_iniciais full_adder_4bits_iniciais_1 (
    .S0(S0), .S1(S1), .S2(S2), .S3(S3), .Cout(full_adder_4bits_iniciais_1_cout), .A(A[3:0]), .B(B[3:0]));
  full_adder_4bits full_adder_4bits_1 (
    .S0(S4), .S1(S5), .S2(S6), .S3(S7), .Cout(full_adder_4bits_1_cout),
    .Cin(full_adder_4bits_iniciais_1_cout), .A(A[7:4]), .B(B[7:4]));
  full_adder_4bits full_adder_4bits_2 (
    .S0(S8), .S1(S9), .S2(S10), .S3(S11), .Cout(full_adder_4bits_2_cout), .Cin(full_adder_4bits_1_cout),
    .A(A[11:8]), .B(B[11:8]));
  full_adder_4bits full_adder_4bits_3 (
    .S0(S12), .S1(S13), .S2(S14), .S3(S15), .Cout(full_adder_4bits_3_cout), .Cin(full_adder_4bits_2_cout),
    .A(A[15:12]), .B(B[15:12]));
  full_adder_4bits full_adder_4bits_4 (
    .S0(S16), .S1(S17), .S2(S18), .S3(S19), .Cout(full_adder_4bits_4_cout), .Cin(full_adder_4bits_3_cout),
    .A(A[19:16]), .B(B[19:16]));
  full_adder_4bits full_adder_4bits_5 (
    .S0(S20), .S1(S21), .S2(S22), .S3(S23), .Cout(full_adder_4bits_5_cout), .Cin(full_adder_4bits_4_cout),
    .A(A[23:20]), .B(B[23:20]));
  full_adder_4bits full_adder_4bits_6 (
    .S0(S24), .S1(S25), .S2(S26), .S3(S27), .Cout(full_adder_4bits_6_cout), .Cin(full_adder_4bits_5_cout),
    .A(A[27:24]), .B(B[27:24]));
  full_adder_4bits_finais full_adder_4bits_finais_1 (
    .S0(S28), .S1(S29), .S2(S30), .S3(S31), .Cin(full_adder_4bits_6_cout), .A(A[31:28]), .B(B[31:28]));
endmodule
