// Digital circuit main.dig as structural Verilog
module main (
  input  clk,
  output [31:0] Display
);

  wire and_1_out, beq, Edisplay, IMMorB_mux, PCmux, stop, Write, zero;
  wire [2:0] Funct;
  wire [23:0] ext_sinal_1__32, full_adder_24bits_1_c, full_adder_24bits_2_c, multiplexer_1_out,
       multiplexer_2_out, multiplexer_3_out, pc_1_out;
  wire [31:0] b_r_1_out1, b_r_1_out_0, ext_zero_1__32, multiplexer_4_out, multiplexer_5_out, rom_1_d, ula_1_c;
  wire [31:24] ext_sinal_1__32_2;

  and and_1 (and_1_out, beq, zero);
  Multiplexer #(.Bits(24)) multiplexer_1 (.sel(stop), .in_0(24'h1), .in_1({24{1'b0}}), .out(multiplexer_1_out));
  Full_Adder_24bits full_adder_24bits_1 (.A(multiplexer_1_out), .B(pc_1_out), .C(full_adder_24bits_1_c));
  Multiplexer #(.Bits(24)) multiplexer_2 (
    .sel(and_1_out), .in_0(full_adder_24bits_1_c), .in_1(full_adder_24bits_2_c), .out(multiplexer_2_out));
  Multiplexer #(.Bits(24)) multiplexer_3 (
    .sel(PCmux), .in_0(multiplexer_2_out), .in_1(full_adder_24bits_2_c), .out(multiplexer_3_out));
  PC pc_1 (.Clk(clk), .In(multiplexer_3_out), .Out(pc_1_out));
  Full_Adder_24bits full_adder_24bits_2 (.A(ext_sinal_1__32), .B(pc_1_out), .C(full_adder_24bits_2_c));
  ROM #(.AddrBits(24), .Bits(32)) rom_1 (.A(pc_1_out), .sel(1'b1), .D(rom_1_d));
  ext_sinal ext_sinal_1 (._16(rom_1_d[15:0]), ._32({ext_sinal_1__32_2, ext_sinal_1__32}));
  ROM #(.AddrBits(4), .Bits(9)) rom_2 (
    .A(rom_1_d[31:28]), .sel(1'b1), .D({PCmux, Funct, IMMorB_mux, Write, Edisplay, beq, stop}));
  B_R b_r_1 (
    .W(Write), .Clk(clk), .In(ula_1_c), .Endw(rom_1_d[19:16]), .End_Ra(rom_1_d[27:24]),
    .End_Rb(rom_1_d[23:20]), .Out_0(b_r_1_out_0), .Out1(b_r_1_out1));
  Multiplexer #(.Bits(32)) multiplexer_4 (.sel(Edisplay), .in_0(Display), .in_1(b_r_1_out_0), .out(multiplexer_4_out));
  ext_zero ext_zero_1 (._16(rom_1_d[15:0]), ._32(ext_zero_1__32));
  Registrador registrador_1 (.Clk(clk), .In(multiplexer_4_out), .Out(Display));
  Multiplexer #(.Bits(32)) multiplexer_5 (
    .sel(IMMorB_mux), .in_0(b_r_1_out1), .in_1(ext_zero_1__32), .out(multiplexer_5_out));
  ULA ula_1 (.A(b_r_1_out_0), .B(multiplexer_5_out), .Seletor(Funct), .C(ula_1_c), .Zero(zero));

  // Notes on the sheet:
  //   clk: Hz: 10
  //   contents of rom_1 (hex, n*v repeats v):
  //   0,9001000a,90020007,90030012,90040000,90050000,c5100007,43560000
  //   ,26260000,24640000,95050001,d4000000,b000fffa,d4000000,e0000000
  //   contents of rom_2 (hex, n*v repeats v):
  //   0,18,8,28,48,68,88,a8,c8,18,38,100,22,4,1
endmodule
