// Digital circuit shifter.dig as structural Verilog
module shifter (
  input  [31:0] A,
  input  [31:0] B,
  output [31:0] C
);

  wire [31:0] multiplexer_1_out, multiplexer_2_out, multiplexer_4_out, multiplexer_5_out, shifter1bit_1_b,
       shifter2bit_1_b, shifter4bit_1_b, shifter16bit_1_b, shifter16bit_2_b, shifter16bit_3_b;

  shifter16bit shifter16bit_1 (.A(multiplexer_2_out), .B(shifter16bit_1_b));
  shifter16bit shifter16bit_2 (.A(shifter16bit_1_b), .B(shifter16bit_2_b));
  shifter1bit shifter1bit_1 (.A(A), .B(shifter1bit_1_b));
  shifter2bit shifter2bit_1 (.A(multiplexer_4_out), .B(shifter2bit_1_b));
  shifter4bit shifter4bit_1 (.A(multiplexer_5_out), .B(shifter4bit_1_b));
  Multiplexer #(.Bits(32)) multiplexer_1 (
    .sel(B[2]), .in_0(multiplexer_5_out), .in_1(shifter4bit_1_b), .out(multiplexer_1_out));
  shifter16bit shifter16bit_3 (.A(multiplexer_1_out), .B(shifter16bit_3_b));
  Multiplexer #(.Bits(32)) multiplexer_2 (
    .sel(B[3]), .in_0(multiplexer_1_out), .in_1(shifter16bit_3_b), .out(multiplexer_2_out));
  Multiplexer #(.Bits(32)) multiplexer_3 (.sel(B[4]), .in_0(multiplexer_2_out), .in_1(shifter16bit_2_b), .out(C));
  Multiplexer #(.Bits(32)) multiplexer_4 (.sel(B[0]), .in_0(A), .in_1(shifter1bit_1_b), .out(multiplexer_4_out));
  Multiplexer #(.Bits(32)) multiplexer_5 (
    .sel(B[1]), .in_0(multiplexer_4_out), .in_1(shifter2bit_1_b), .out(multiplexer_5_out));
endmodule
