// Digital circuit shifter16bit.dig as structural Verilog
module shifter16bit (
  input  [31:0] A,
  output [31:0] B
);

  wire [31:0] shifter8bit_1_b;

  shifter8bit shifter8bit_1 (.A(A), .B(shifter8bit_1_b));
  shifter8bit shifter8bit_2 (.A(shifter8bit_1_b), .B(B));
endmodule
