// Digital circuit shifter2bit.dig as structural Verilog
module shifter2bit (
  input  [31:0] A,
  output [31:0] B
);

  wire [31:0] shifter1bit_1_b;

  shifter1bit shifter1bit_1 (.A(A), .B(shifter1bit_1_b));
  shifter1bit shifter1bit_2 (.A(shifter1bit_1_b), .B(B));
endmodule
