// Digital circuit shifter4bit.dig as structural Verilog
module shifter4bit (
  input  [31:0] A,
  output [31:0] B
);

  wire [31:0] shifter2bit_1_b;

  shifter2bit shifter2bit_1 (.A(A), .B(shifter2bit_1_b));
  shifter2bit shifter2bit_2 (.A(shifter2bit_1_b), .B(B));
endmodule
