// Digital circuit shifter8bit.dig as structural Verilog
module shifter8bit (
  input  [31:0] A,
  output [31:0] B
);

  wire [31:0] shifter4bit_1_b;

  shifter4bit shifter4bit_1 (.A(A), .B(shifter4bit_1_b));
  shifter4bit shifter4bit_2 (.A(shifter4bit_1_b), .B(B));
endmodule
